# Fritzing sketch fight-vest-scatch (saved by Fritzing 0.9.3b)
breadboards: 1

parts:
  Part1 = Arduino Uno (Rev3)
  Part2 = Bluetooth HC-05 Macho
  VCC1 = Battery block 9V
  R1 = Resistor [tolerance=±5% resistance=220 package="1206 [SMD]"]
  R2 = Resistor [tolerance=±5% resistance=220 package="2010 [SMD]"]
  R3 = Resistor [tolerance=±5% resistance=220 package="2512 [SMD]"]

nets:
  N1: Part1.D0/RX, Part2.TXD
  N2: Part1.D1/TX, R3.Pin_1
  5V: Part1.5V, Part2.VCC
  GND: Part1.GND, Part2.GND, VCC1.-, R1.Pin_0
  N3: Part1.VIN, VCC1.+
  N4: Part2.RXD, R2.Pin_1, R3.Pin_0
  N5: R1.Pin_1, R2.Pin_0
